# Fritzing sketch Arduino transmitter (saved by Fritzing 0.9.3b)
breadboards: 1

parts:
  Part1 = Arduino Uno (Rev3)
  Part2 = Arduino XBee Shield
  LED1 = LED - 5mm [color="Red (633nm)" package="5 mm [THT]"]
  HC-SR04_Sensor_1 = HC-SR04 Ultrasonic Distance Sensor

nets:
  N1: Part1.D8, LED1.anode
  N2: Part1.D11_PWM/MOSI, Part2.UART_TX
  N3: Part1.D12/MISO, Part2.UART_RX
  GND: Part1.GND, Part2.GND, LED1.cathode, HC-SR04_Sensor_1.GND
  N4: Part1.D6_PWM, HC-SR04_Sensor_1.TRIG
  N5: Part1.D7, HC-SR04_Sensor_1.ECHO
  5V: Part1.5V, Part2.5V, HC-SR04_Sensor_1.VCC

notes:
  xBee Shield
  Ultrasonic distance
  sensor
  Arduino Uno
  Red LED

// code stored in the sketch: sonar_sensor_final.ino
// This program receives the proximity sensor data from an Arduino sonar sensor and displays it on the serial monitor
// We include the Software serial library in order to receive data from another Arduino
# include <SoftwareSerial.h>

// String were we'll store the receive data
String receive;

// xBee Transmitter Tx and Rx ports
short xBeeTx = 11;
short xBeeRx = 12;

// We define the xBeeSerial object
SoftwareSerial xBeeSerial(xBeeRx, xBeeTx);

// Code setup
void setup (){
  
  Serial.begin(9600);
  xBeeSerial.begin (9600) ;
  
}// End void setup ()

// Code loop
void loop (){

  // If we receive data we print it out.
  if (xBeeSerial.available() > 0){
    receive = xBeeSerial.readStringUntil('\n'); // read in data as a String
    //int receiveInt = receive.toInt(); // convert a String into an integer
    Serial.println(receive );
  }// End if (xBeeSerial.available() > 0)
  
}//End void loop ()
